# Fritzing sketch led-with-pot (saved by Fritzing 0.9.3b)
breadboards: 1

parts:
  BAT = Battery Holders [package=battcom_20mm_pth]
  R1 = Resistor [tolerance=±5% resistance=100 package=THT]
  LED1 = LED - 5mm [color="Red (633nm)" package="5 mm [THT]"]
  R2 = Rotary Potentiometer (Small) [maximum_resistance=10kΩ package=THT]

nets:
  N1: BAT.+, R1.Pin_0
  N2: BAT.-, R2.wiper
  N3: R1.Pin_1, LED1.anode
  N4: LED1.cathode, R2.leg2
