# Fritzing sketch light-sensor (saved by Fritzing 0.9.3b)
breadboards: 1

parts:
  R1 = Resistor [tolerance=±5% resistance=100 package=THT]
  LED1 = LED - 5mm [color="Red (633nm)" package="5 mm [THT]"]
  Part1 = Arduino Uno (Rev3) - ICSP
  R2 = Resistor [tolerance=±5% resistance=100k package=THT]
  R3 = Photocell (LDR) [package=THT]

nets:
  N1: R1.Pin_0, Part1.D3_PWM
  N2: R1.Pin_1, LED1.anode
  GND: LED1.cathode, R2.Pin_1
  N3: Part1.A0, R2.Pin_0, R3.pin_1
  N4: Part1.5V, R3.pin_0
