# Fritzing sketch arduino-schematic (saved by Fritzing 0.9.3b)
breadboards: 1

parts:
  Arduino = Arduino Uno (Rev3) - ICSP
  S1 = Pushbutton [package="[THT]"]
  R1 = Resistor [tolerance=±5% resistance=10k package=THT]
  R2 = Resistor [tolerance=±5% resistance=300 package=THT]
  LED1 = LED - 5mm [color="Red (633nm)" package="5 mm [THT]"]
  J1 = Piezo Speaker

nets:
  N1: Arduino.A0, S1.Pin_3, S1.Pin_4, R1.Pin_0
  N2: Arduino.A2, J1.pin2
  N3: Arduino.GND, R1.Pin_1, LED1.cathode, J1.pin1
  N4: Arduino.5V, S1.Pin_1, S1.Pin_2
  N5: Arduino.D2, R2.Pin_0
  N6: R2.Pin_1, LED1.anode
