# Fritzing sketch attiny-complete (saved by Fritzing 0.9.3b)
breadboards: 1

parts:
  S2 = Pushbutton [package="[THT]"]
  R3 = Resistor [tolerance=±5% resistance=10k package=THT]
  R4 = Resistor [tolerance=±5% resistance=300 package=THT]
  LED2 = LED - 5mm [color="Red (633nm)" package="5 mm [THT]"]
  J2 = Piezo Speaker
  U1 = attiny85 [package=dip]
  VCC1 = Battery

nets:
  N1: S2.Pin_1, R3.Pin_0, U1.Pin_2
  3V: S2.Pin_3, S2.Pin_4, U1.Pin_8, VCC1.+
  GND: R3.Pin_1, LED2.cathode, J2.pin1, U1.Pin_4, VCC1.-
  N2: R4.Pin_0, U1.Pin_6
  N3: R4.Pin_1, LED2.anode
  N4: J2.pin2, U1.Pin_5
